// Logisim project 7_segment.circ as structural Verilog: 1 circuit, main circuit main
module main (
);

  wire dipswitch_1_sw1, dipswitch_1_sw2, dipswitch_1_sw3, dipswitch_1_sw4, dipswitch_1_sw5, dipswitch_1_sw6,
       dipswitch_1_sw7, dipswitch_1_sw8;

  _7_Segment_Display u_7_segment_display_1 (
    .g(dipswitch_1_sw8), .f(dipswitch_1_sw7), .a(dipswitch_1_sw6), .b(dipswitch_1_sw5), .e(dipswitch_1_sw1),
    .d(dipswitch_1_sw2), .c(dipswitch_1_sw3), .dp(dipswitch_1_sw4));
  DipSwitch dipswitch_1 (
    .sw1(dipswitch_1_sw1), .sw2(dipswitch_1_sw2), .sw3(dipswitch_1_sw3), .sw4(dipswitch_1_sw4),
    .sw5(dipswitch_1_sw5), .sw6(dipswitch_1_sw6), .sw7(dipswitch_1_sw7), .sw8(dipswitch_1_sw8));
endmodule
