// Logisim project Lab2v1.circ as structural Verilog: 1 circuit, main circuit main
module main (
  input  A,
  input  B,
  input  C,
  input  D,
  output out_5,
  output out_6
);

  wire AB_out, ABC_out, ABD_out, AC_out, ACD_out, AD_out, BC_out, BCD_out, BD_out, CD_out;

  and AB (AB_out, A, B);
  and AC (AC_out, A, C);
  and AD (AD_out, A, D);
  and BC (BC_out, B, C);
  and BD (BD_out, B, D);
  and CD (CD_out, C, D);
  and ABC (ABC_out, AB_out, AC_out);
  and ABD (ABD_out, AB_out, AD_out);
  and BCD (BCD_out, BC_out, BD_out);
  and ACD (ACD_out, AC_out, CD_out);
  ExactlyOne xor_1 (.out(out_5), .in0(AB_out), .in1(AC_out), .in2(AD_out), .in3(BC_out), .in4(BD_out), .in5(CD_out));
  ExactlyOne xor_2 (.out(out_6), .in0(ABC_out), .in1(ABD_out), .in2(BCD_out), .in3(ACD_out));

  // Notes on the sheet:
  //   AC
  //   CD
  //   AB
  //   AD
  //   BC
  //   BD
  //   AB
  //   AC
  //   AB
  //   AC
  //   AD
  //   BC
  //   BD
  //   CD
  //   ABC
  //   ABD
  //   BCD
  //   ACD
  //   T
  //   P
  //    = ((AB) ⊕ (AC) ⊕ (AD) ⊕ (BC) ⊕ (BD) ⊕ (CD) )
  //   T = ((ABCD') ⊕ (ABC'D) ⊕ (AB'CD) ⊕ (A'BCD))
  //   = ((ABC) ⊕ (ABD) ⊕ (ACD) ⊕ (BCD))
  //   P = ((ABC'D') ⊕ (AB'CD') ⊕ (AB'C'D) ⊕ (A'BCD') ⊕ (A'BC'D) ⊕ (A'B'CD))
endmodule
