// Logisim project Lab01.circ as structural Verilog: 1 circuit, main circuit main
module main (
  input  A,
  input  B,
  output C
);

  wire not_1_out;

  not not_1 (not_1_out, B);
  and and_1 (C, A, not_1_out);

  // Notes on the sheet:
  //   A
  //   B'
  //   A*B'
endmodule
