// Logisim project Version_1.circ as structural Verilog: 1 circuit, main circuit main
module main (
  input  A0,
  input  A1,
  input  B0,
  input  B1,
  output C0,
  output C1
);

  wire and_1_out, and_2_out, and_3_out, and_4_out, and_5_out, and_6_out, and_7_out, and_8_out, not_1_out,
       not_2_out, not_3_out, not_4_out, not_5_out, not_6_out, or_1_out;

  not not_1 (not_1_out, B1);
  not not_2 (not_2_out, A1);
  and and_1 (and_1_out, A0, not_1_out);
  and and_2 (and_2_out, not_2_out, B0);
  not not_3 (not_3_out, A0);
  not not_4 (not_4_out, B0);
  not not_5 (not_5_out, A1);
  not not_6 (not_6_out, B1);
  and and_3 (and_3_out, not_3_out, A1);
  and and_4 (and_4_out, not_4_out, B1);
  and and_5 (and_5_out, and_1_out, not_5_out);
  and and_6 (and_6_out, and_2_out, not_6_out);
  and and_7 (and_7_out, B0, B1);
  and and_8 (and_8_out, A1, A0);
  or or_1 (or_1_out, and_7_out, and_8_out);
  or or_2 (C1, and_3_out, or_1_out, and_4_out);
  or or_3 (C0, and_5_out, or_1_out, and_6_out);

  // Notes on the sheet:
  //   Value = 1
endmodule
