// Logisim project Version_2.circ as structural Verilog: 1 circuit, main circuit main
module main (
  input  A1,
  input  A0,
  input  B1,
  input  B0,
  output C1,
  output C0
);

  wire and_1_out, and_2_out, not_1_out, not_2_out, or_1_out, or_2_out;

  not not_1 (not_1_out, B1);
  not not_2 (not_2_out, A1);
  or or_1 (or_1_out, A1, not_1_out);
  or or_2 (or_2_out, not_2_out, B1);
  or or_3 (C1, B1, A1);
  and and_1 (and_1_out, A0, or_1_out);
  and and_2 (and_2_out, or_2_out, B0);
  or or_4 (C0, and_1_out, and_2_out);

  // Notes on the sheet:
  //   A1
  //   B1
  //   B1
  //   A0
  //   A1
  //   B1'
  //   A1'
  //   B1
  //   A1 + B1'
  //   A1' + B1
  //   B0
  //   A1 + B1
  //   A0(A1 + B1')
  //   B0(A1' + B1)
  //   = A1 + B1
  //   = A0(A1 + B1') + B0(A1' + B1)
endmodule
