// Logisim project Version_1.circ as structural Verilog: 9 circuits, main circuit design0
module design0 (
  input  A1,
  input  A0,
  input  B1,
  input  B0,
  output C1,
  output C0
);

  wire and_1_out, and_2_out, not_1_out, not_2_out, or_1_out, or_2_out;

  not not_1 (not_1_out, B1);
  not not_2 (not_2_out, A1);
  or or_1 (or_1_out, A1, not_1_out);
  or or_2 (or_2_out, not_2_out, B1);
  or or_3 (C1, B1, A1);
  and and_1 (and_1_out, A0, or_1_out);
  and and_2 (and_2_out, or_2_out, B0);
  or or_4 (C0, and_1_out, and_2_out);

  // Notes on the sheet:
  //   A1
  //   B1
  //   B1
  //   A0
  //   A1
  //   B1'
  //   A1'
  //   B1
  //   A1 + B1'
  //   A1' + B1
  //   B0
  //   A1 + B1
  //   A0(A1 + B1')
  //   B0(A1' + B1)
  //   = A1 + B1
  //   = A0(A1 + B1') + B0(A1' + B1)
endmodule

module design1 (
  input  A1,
  input  A0,
  input  B1,
  input  B0,
  output C1,
  output C0
);

  Multiplexer #(.select(4)) multiplexer_1 (
    .in0(1'b0), .in1(1'b0), .in2(1'b1), .in3(1'b1), .in4(1'b0), .in5(1'b0), .in6(1'b1), .in7(1'b1),
    .in8(1'b1), .in9(1'b1), .in10(1'b1), .in11(1'b1), .in12(1'b1), .in13(1'b1), .in14(1'b1), .in15(1'b1),
    .out(C1), .sel({A1, A0, B1, B0}));
  Multiplexer #(.select(4)) multiplexer_2 (
    .in0(1'b0), .in1(1'b1), .in2(1'b0), .in3(1'b1), .in4(1'b1), .in5(1'b1), .in6(1'b0), .in7(1'b1),
    .in8(1'b0), .in9(1'b0), .in10(1'b0), .in11(1'b1), .in12(1'b1), .in13(1'b1), .in14(1'b1), .in15(1'b1),
    .out(C0), .sel({A1, A0, B1, B0}));
endmodule

module design2 (
  input  A1,
  input  A0,
  input  B1,
  input  B0,
  output C1,
  output C0
);

  wire multiplexer_1_out, multiplexer_2_out, multiplexer_3_out, multiplexer_4_out, multiplexer_6_out,
       multiplexer_7_out;

  Multiplexer multiplexer_1 (.in0(1'b1), .in1(1'b0), .out(multiplexer_1_out), .sel(B1));
  Multiplexer multiplexer_2 (.in0(1'b1), .in1(1'b0), .out(multiplexer_2_out), .sel(A1));
  Multiplexer multiplexer_3 (.in0(multiplexer_1_out), .in1(1'b1), .out(multiplexer_3_out), .sel(A1));
  Multiplexer multiplexer_4 (.in0(multiplexer_2_out), .in1(1'b1), .out(multiplexer_4_out), .sel(B1));
  Multiplexer multiplexer_5 (.in0(B1), .in1(1'b1), .out(C1), .sel(A1));
  Multiplexer multiplexer_6 (.in0(1'b0), .in1(A0), .out(multiplexer_6_out), .sel(multiplexer_3_out));
  Multiplexer multiplexer_7 (.in0(1'b0), .in1(B0), .out(multiplexer_7_out), .sel(multiplexer_4_out));
  Multiplexer multiplexer_8 (.in0(multiplexer_6_out), .in1(1'b1), .out(C0), .sel(multiplexer_7_out));

  // Notes on the sheet:
  //   NOT Logic
  //   B1
  //   A1
  //   B1
  //   A1
  //   B1'
  //   A1
  //   A1'
  //   B1
  //   OR Logic
  //   A1 + B1'
  //   A1' + B1
  //   OR Logic
  //   A1 + B1
  //   A0
  //   B0
  //   AND Logic
  //   A0A1 + A0B1'
  //   B0A1' + B0B1
  //   OR Logic
  //   A1 + B1
  //   A0A1 + A0B1' + B0A1' + B0B1
endmodule

module design3 (
  input  A1,
  input  A0,
  input  B1,
  input  B0,
  output C1,
  output C0
);

  wire nand_1_out, nand_2_out, nand_3_out, nand_4_out, nand_5_out, nand_6_out, nand_7_out, nand_8_out,
       nand_9_out, nand_10_out, nand_11_out, nand_12_out, nand_13_out, nand_14_out, nand_15_out, nand_16_out;

  nand nand_1 (nand_1_out, B1, B1);
  nand nand_2 (nand_2_out, A1, A1);
  nand nand_3 (nand_3_out, A1, A1);
  nand nand_4 (nand_4_out, nand_1_out, nand_1_out);
  nand nand_5 (nand_5_out, nand_2_out, nand_2_out);
  nand nand_6 (nand_6_out, B1, B1);
  nand nand_7 (nand_7_out, nand_3_out, nand_4_out);
  nand nand_8 (nand_8_out, nand_5_out, nand_6_out);
  nand nand_9 (nand_9_out, A0, nand_7_out);
  nand nand_10 (nand_10_out, nand_8_out, B0);
  nand nand_11 (nand_11_out, nand_9_out, nand_9_out);
  nand nand_12 (nand_12_out, nand_10_out, nand_10_out);
  nand nand_13 (nand_13_out, B1, B1);
  nand nand_14 (nand_14_out, A1, A1);
  nand nand_15 (nand_15_out, nand_11_out, nand_11_out);
  nand nand_16 (nand_16_out, nand_12_out, nand_12_out);
  nand nand_17 (C1, nand_13_out, nand_14_out);
  nand nand_18 (C0, nand_15_out, nand_16_out);

  // Notes on the sheet:
  //   B1
  //   A1
  //   NOT Logic
  //   B0
  //   A1
  //   B1'
  //   A1'
  //   B1
  //   B1
  //   A1
  //   OR Logic
  //   A1'
  //   B1
  //   A1
  //   B1'
  //   A0
  //   A1 + B1'
  //   A1' + B1
  //   AND Logic
  //   A0A1 + A0B1'
  //   A1'B0 + B0B1
  //   B1'
  //   A1'
  //   OR Logic
  //   A1 + B1
  //   A1 + B1
  //   A0A1 + A0B1' + B0A1' + B0B1
endmodule

module design4 (
  input  A,
  input  B,
  input  [1:0] MSG_IN,
  output [1:0] MSG_OUT
);

  wire [1:0] multiplexer_1_out;

  Multiplexer #(.select(2), .width(2)) multiplexer_1 (
    .in0(2'b00), .in1(2'b10), .in2(2'b01), .in3(2'b00), .out(multiplexer_1_out), .sel({A, B}));
  Multiplexer #(.select(2), .width(2)) multiplexer_2 (
    .in0(multiplexer_1_out), .in1(MSG_IN), .in2(MSG_IN), .in3(multiplexer_1_out), .out(MSG_OUT), .sel(MSG_IN));

  // Notes on the sheet:
  //   SEL_MUX
  //   MSG_MUX Logic
  //   01 | A is Larger - Passes 01 to MSG_OUT
  //   10 | B is Larger - Passes 10 is MSG_OUT
  //   00 | Tie - Passes SEL_MUX value to MSG_OUT
  //   11 | Invalid output - Passes SEL_MUX value to MSG_OUT
endmodule

module design5 (
  input  [3:0] A,
  input  [3:0] B,
  output [3:0] C
);

  wire [1:0] design4_1_msg_out, design4_2_msg_out, design4_3_msg_out, design4_4_msg_out;

  design4 design4_1 (.A(A[3]), .B(B[3]), .MSG_IN(2'b00), .MSG_OUT(design4_1_msg_out));
  design4 design4_2 (.A(A[2]), .B(B[2]), .MSG_IN(design4_1_msg_out), .MSG_OUT(design4_2_msg_out));
  design4 design4_3 (.A(A[1]), .B(B[1]), .MSG_IN(design4_2_msg_out), .MSG_OUT(design4_3_msg_out));
  Multiplexer #(.select(2), .width(4)) multiplexer_1 (
    .in0(A), .in1(A), .in2(B), .in3(B), .out(C), .sel(design4_4_msg_out));
  design4 design4_4 (.A(A[0]), .B(B[0]), .MSG_IN(design4_3_msg_out), .MSG_OUT(design4_4_msg_out));

  // Notes on the sheet:
  //   Begin MSG_IN
  //   Bit 3 Compare
  //   Bit 2 Compare
  //   Bit 1 Compare
  //   Outputs greater value
  //   MUX Select Bit:
  //   00 | Tie
  //   01 | A is greater
  //   10 | B is greater
  //   Bit 0 Compare
  //   11 | Invalid output
endmodule

module circuit_guide (
  input  I3,
  input  in_2,
  input  I2,
  input  in_4,
  input  I1,
  input  in_6,
  input  I0,
  input  in_8,
  input  in_9,
  input  I4,
  input  A,
  input  B,
  input  [1:0] message_in,
  output AND1,
  output out_15,
  output OR1,
  output out_17,
  output NOT1,
  output out_19
);

  wire nand_1_out, nand_2_out, nand_3_out;

  // AND_Gate and_1 is placed but not wired
  // OR_Gate or_1 is placed but not wired
  // NOT_Gate not_1 is placed but not wired
  Multiplexer multiplexer_1 (.in0(1'b0), .in1(I3), .out(AND1), .sel(I2));
  Multiplexer multiplexer_2 (.in0(I1), .in1(1'b1), .out(OR1), .sel(I0));
  Multiplexer multiplexer_3 (.in0(1'b1), .in1(1'b0), .out(NOT1), .sel(I4));
  nand nand_1 (nand_1_out, in_2, in_4);
  nand nand_2 (nand_2_out, in_6, in_6);
  nand nand_3 (nand_3_out, in_8, in_8);
  nand nand_4 (out_19, in_9, in_9);
  nand nand_5 (out_15, nand_1_out, nand_1_out);
  nand nand_6 (out_17, nand_2_out, nand_3_out);
  Multiplexer #(.select(2)) multiplexer_4 (.sel({A, B}));  // open: in0, in1, in2, in3, out

  // Notes on the sheet:
  //   AND Logic
  //   OR Logic
  //   NOT Logic
  //   MUX Device Implementation
  //   NAND Device Implementation
endmodule

module design6 (
  input  [3:0] A,
  input  [3:0] B,
  input  [1:0] MSG_IN,
  output [1:0] MSG_OUT
);

  wire [1:0] design4_1_msg_out, design4_2_msg_out, design4_3_msg_out;

  design4 design4_1 (.A(A[3]), .B(B[3]), .MSG_IN(MSG_IN), .MSG_OUT(design4_1_msg_out));
  design4 design4_2 (.A(A[2]), .B(B[2]), .MSG_IN(design4_1_msg_out), .MSG_OUT(design4_2_msg_out));
  design4 design4_3 (.A(A[1]), .B(B[1]), .MSG_IN(design4_2_msg_out), .MSG_OUT(design4_3_msg_out));
  design4 design4_4 (.A(A[0]), .B(B[0]), .MSG_IN(design4_3_msg_out), .MSG_OUT(MSG_OUT));

  // Notes on the sheet:
  //   Bit 3 Compare
  //   Bit 2 Compare
  //   Bit 1 Compare
  //   Outputs greater value
  //   Bit 0 Compare
endmodule

module circ32 (
  input  [31:0] A,
  input  [31:0] B,
  input  [1:0] in_3,
  output [31:0] C
);

  wire [1:0] design6_1_msg_out, design6_2_msg_out, design6_3_msg_out, design6_4_msg_out, design6_5_msg_out,
       design6_6_msg_out, design6_7_msg_out, design6_8_msg_out;

  design6 design6_1 (.A(A[31:28]), .B(B[31:28]), .MSG_IN(in_3), .MSG_OUT(design6_1_msg_out));
  design6 design6_2 (.A(A[15:12]), .B(B[15:12]), .MSG_IN(design6_7_msg_out), .MSG_OUT(design6_2_msg_out));
  design6 design6_3 (.A(A[27:24]), .B(B[27:24]), .MSG_IN(design6_1_msg_out), .MSG_OUT(design6_3_msg_out));
  design6 design6_4 (.A(A[11:8]), .B(B[11:8]), .MSG_IN(design6_2_msg_out), .MSG_OUT(design6_4_msg_out));
  design6 design6_5 (.A(A[23:20]), .B(B[23:20]), .MSG_IN(design6_3_msg_out), .MSG_OUT(design6_5_msg_out));
  design6 design6_6 (.A(A[7:4]), .B(B[7:4]), .MSG_IN(design6_4_msg_out), .MSG_OUT(design6_6_msg_out));
  design6 design6_7 (.A(A[19:16]), .B(B[19:16]), .MSG_IN(design6_5_msg_out), .MSG_OUT(design6_7_msg_out));
  design6 design6_8 (.A(A[3:0]), .B(B[3:0]), .MSG_IN(design6_6_msg_out), .MSG_OUT(design6_8_msg_out));
  Multiplexer #(.select(2), .width(32)) multiplexer_1 (
    .in0(A), .in1(A), .in2(B), .in3(B), .out(C), .sel(design6_8_msg_out));

  // Notes on the sheet:
  //   Outputs greater value
  //   00 | Tie
  //   MUX Select Bit:
  //   01 | A is greater
  //   10 | B is greater
endmodule
