// Logisim project Lab5_notes.circ as structural Verilog: 4 circuits, main circuit main
module main (
  input  in_1,
  input  In,
  input  E,
  output out_4,
  output Shot,
  output T
);

  wire and_1_out, and_2_out, clock_1_out, clock_2_out, clock_3_out, d_ff_1_qn, d_ff_2_q, d_ff_3_qn,
       not_1_out, or_2_out;

  Clock clock_1 (.out(clock_1_out));
  Clock clock_2 (.out(clock_2_out));
  Clock clock_3 (.out(clock_3_out));
  D_Flip_Flop d_ff_1 (.D(in_1), .clk(clock_1_out), .Q(out_4), .Qn(d_ff_1_qn));  // open: preset, reset
  D_Flip_Flop d_ff_2 (.D(Shot), .clk(clock_2_out), .Q(d_ff_2_q));  // open: Qn, preset, reset
  D_Flip_Flop d_ff_3 (.D(or_2_out), .clk(clock_3_out), .Q(T), .Qn(d_ff_3_qn));  // open: preset, reset
  or or_1 (Shot, In, d_ff_2_q);
  not not_1 (not_1_out, E);
  and and_1 (and_1_out, not_1_out, T);
  and and_2 (and_2_out, E, d_ff_3_qn);
  or or_2 (or_2_out, and_1_out, and_2_out);

  // Notes on the sheet:
  //   Basic D Flip Flop
  //   Mealy Device
  //   Moore Device
  //   Shot = In + Q
  //   Q* = In + Q
  //   T = Q
  //   Q* = E'Q + EQ'
endmodule

module figure_1 (
  input  In,
  output Shot
);

  wire clock_1_out, d_ff_1_q;

  Clock clock_1 (.out(clock_1_out));
  D_Flip_Flop d_ff_1 (.D(Shot), .clk(clock_1_out), .Q(d_ff_1_q));  // open: Qn, preset, reset
  or or_1 (Shot, In, d_ff_1_q);

  // Notes on the sheet:
  //   Mealy Device
  //   Shot = In + Q
  //   Q* = In + Q
endmodule

module figure_2 (
  input  E,
  output T
);

  wire and_1_out, and_2_out, clock_1_out, d_ff_1_qn, not_1_out, or_1_out;

  Clock clock_1 (.out(clock_1_out));
  D_Flip_Flop d_ff_1 (.D(or_1_out), .clk(clock_1_out), .Q(T), .Qn(d_ff_1_qn));  // open: preset, reset
  not not_1 (not_1_out, E);
  and and_1 (and_1_out, not_1_out, T);
  and and_2 (and_2_out, E, d_ff_1_qn);
  or or_1 (or_1_out, and_1_out, and_2_out);

  // Notes on the sheet:
  //   Moore Device
  //   T = Q
  //   Q* = E'Q + EQ'
endmodule

module figure_3 (
  input  X,
  output Unlock
);

  wire and_1_out, and_2_out, and_3_out, and_5_out, clock_1_out, d_ff_1_q, d_ff_1_qn, d_ff_2_q, d_ff_2_qn,
       not_1_out, or_1_out, or_2_out;

  Clock clock_1 (.out(clock_1_out));
  not not_1 (not_1_out, X);
  D_Flip_Flop d_ff_1 (.D(or_2_out), .clk(clock_1_out), .Q(d_ff_1_q), .Qn(d_ff_1_qn));  // open: preset, reset
  D_Flip_Flop d_ff_2 (.D(or_1_out), .clk(clock_1_out), .Q(d_ff_2_q), .Qn(d_ff_2_qn));  // open: preset, reset
  and and_1 (and_1_out, X, d_ff_1_qn);
  and and_2 (and_2_out, X, d_ff_2_q);
  and and_3 (and_3_out, d_ff_2_q, d_ff_1_qn);
  and and_4 (Unlock, d_ff_2_qn, d_ff_1_q);
  and and_5 (and_5_out, d_ff_2_q, not_1_out);
  or or_1 (or_1_out, and_1_out, and_2_out, and_3_out);
  or or_2 (or_2_out, Unlock, and_5_out);
endmodule
