// Logisim project lab7.circ as structural Verilog: 4 circuits, main circuit main
module main (
  input  I,
  output out_2
);

  wire and_2_out, and_3_out, and_4_out, and_5_out, clock_1_out, nand_1_out, not_1_out, or_1_out, Q0_q, Q1_q,
       Q1_qn, Q2_q, Q2_qn, xor_1_out;

  Clock clock_1 (.out(clock_1_out));
  not not_1 (not_1_out, I);
  D_Flip_Flop Q2 (.D(I), .clk(clock_1_out), .Q(Q2_q), .Qn(Q2_qn));  // open: preset, reset
  D_Flip_Flop Q1 (.D(nand_1_out), .clk(clock_1_out), .Q(Q1_q), .Qn(Q1_qn));  // open: preset, reset
  D_Flip_Flop Q0 (.D(or_1_out), .clk(clock_1_out), .Q(Q0_q));  // open: Qn, preset, reset
  xor xor_1 (xor_1_out, Q2_q, Q0_q);
  and and_1 (out_2, xor_1_out, Q1_q);
  and and_2 (and_2_out, Q0_q, Q1_qn, Q2_qn, I);
  and and_3 (and_3_out, Q2_q, not_1_out);
  and and_4 (and_4_out, and_3_out, Q0_q);
  and and_5 (and_5_out, Q1_q, Q2_qn);
  nand nand_1 (nand_1_out, ~and_2_out, ~and_3_out);  // NAND_Gate
  or or_1 (or_1_out, and_4_out, and_5_out);
endmodule

module moore_implementation (
  input  I,
  output Unlock
);

  wire and_1_out, and_2_out, and_3_out, and_4_out, and_5_out, and_6_out, and_7_out, and_8_out, and_9_out,
       and_10_out, and_11_out, and_12_out, and_13_out, and_14_out, and_15_out, and_16_out, clock_1_out,
       not_1_out, or_1_out, or_2_out, or_3_out, or_4_out, or_5_out, or_6_out, or_7_out, or_8_out, Q0_q,
       Q0_qn, Q1_q, Q1_qn, Q2_q, Q2_qn;

  Clock clock_1 (.out(clock_1_out));
  not not_1 (not_1_out, I);
  and and_1 (and_1_out, Q2_q, Q1_qn);
  and and_2 (and_2_out, not_1_out, Q0_q);
  and and_3 (and_3_out, I, Q0_qn);
  and and_4 (and_4_out, Q1_qn, Q2_q);
  and and_5 (and_5_out, Q2_qn, Q1_qn);
  and and_6 (and_6_out, Q0_q, Q1_qn);
  and and_7 (and_7_out, Q1_q, Q0_qn);
  and and_8 (and_8_out, not_1_out, Q2_q, Q1_q);
  and and_9 (and_9_out, I, or_1_out);
  or or_1 (or_1_out, Q2_qn, and_1_out);
  or or_2 (or_2_out, and_2_out, and_3_out);
  and and_10 (and_10_out, or_2_out, and_4_out);
  and and_11 (and_11_out, Q1_q, Q0_qn, not_1_out);
  and and_12 (and_12_out, Q1_q, Q0_q, I);
  and and_13 (and_13_out, Q0_q, or_3_out);
  or or_3 (or_3_out, I, and_5_out);
  and and_14 (and_14_out, Q2_q, or_4_out);
  or or_4 (or_4_out, and_6_out, and_7_out);
  or or_5 (or_5_out, and_8_out, and_9_out);
  and and_15 (and_15_out, Q0_qn, or_5_out);
  and and_16 (and_16_out, not_1_out, Q0_q, Q1_qn);
  D_Flip_Flop Q2 (.D(or_6_out), .clk(clock_1_out), .Q(Q2_q), .Qn(Q2_qn));  // open: preset, reset
  or or_6 (or_6_out, and_10_out, and_11_out, and_12_out);
  D_Flip_Flop Q1 (.D(or_7_out), .clk(clock_1_out), .Q(Q1_q), .Qn(Q1_qn));  // open: preset, reset
  or or_7 (or_7_out, and_13_out, and_14_out);
  D_Flip_Flop Q0 (.D(or_8_out), .clk(clock_1_out), .Q(Q0_q), .Qn(Q0_qn));  // open: preset, reset
  or or_8 (or_8_out, and_15_out, and_16_out);
  and and_17 (Unlock, Q2_q, Q0_q);

  // Notes on the sheet:
  //   =Q2Q0
endmodule

module mealy_implementation (
  input  I,
  output Unlock
);

  wire and_1_out, and_2_out, and_3_out, and_4_out, and_5_out, and_6_out, and_7_out, and_8_out, clock_1_out,
       not_1_out, or_1_out, or_2_out, or_3_out, or_4_out, Q0_q, Q0_qn, Q1_q, Q1_qn, Q2_q, Q2_qn, xor_1_out,
       xor_2_out, xor_3_out, xor_4_out;

  Clock clock_1 (.out(clock_1_out));
  not not_1 (not_1_out, I);
  xor xor_1 (xor_1_out, Q2_q, Q1_q);
  and and_1 (and_1_out, xor_1_out, Q0_q, I);
  and and_2 (and_2_out, not_1_out, Q0_qn, Q1_q, Q2_qn);
  and and_3 (and_3_out, Q2_qn, Q1_q, I, Q0_qn);
  and and_4 (and_4_out, Q1_qn, xor_2_out);
  xor xor_2 (xor_2_out, Q2_q, Q0_qn);
  xor xor_3 (xor_3_out, I, Q0_q);
  xor xor_4 (xor_4_out, Q2_q, Q1_q);
  or or_1 (or_1_out, and_1_out, and_2_out);
  or or_2 (or_2_out, and_3_out, and_4_out);
  and and_5 (and_5_out, xor_3_out, Q1_q, Q2_qn);
  or or_3 (or_3_out, and_5_out, and_6_out);
  and and_6 (and_6_out, not_1_out, Q0_qn, xor_4_out);
  D_Flip_Flop Q2 (.D(or_1_out), .clk(clock_1_out), .Q(Q2_q), .Qn(Q2_qn));  // open: preset, reset
  D_Flip_Flop Q1 (.D(or_2_out), .clk(clock_1_out), .Q(Q1_q), .Qn(Q1_qn));  // open: preset, reset
  D_Flip_Flop Q0 (.D(or_3_out), .clk(clock_1_out), .Q(Q0_q), .Qn(Q0_qn));  // open: preset, reset
  and and_7 (and_7_out, I, Q0_q);
  and and_8 (and_8_out, not_1_out, Q0_qn);
  or or_4 (or_4_out, and_7_out, and_8_out);
  and and_9 (Unlock, or_4_out, Q2_q, Q1_qn);
endmodule

module mealy_v2 (
  input  I,
  output Unlock
);

  wire and_1_out, and_2_out, and_3_out, and_4_out, and_5_out, and_6_out, and_7_out, and_8_out, and_9_out,
       and_10_out, and_11_out, and_12_out, and_13_out, and_14_out, and_15_out, and_16_out, and_17_out,
       and_18_out, and_19_out, clock_1_out, d_ff_1_q, d_ff_1_qn, d_ff_2_q, d_ff_2_qn, d_ff_3_q, d_ff_3_qn,
       not_1_out, or_1_out, or_2_out, or_3_out, or_4_out, or_5_out, or_6_out, or_7_out;

  not not_1 (not_1_out, I);
  Clock clock_1 (.out(clock_1_out));
  and and_1 (and_1_out, d_ff_2_q, d_ff_1_qn);
  and and_2 (and_2_out, d_ff_2_qn, d_ff_2_q);
  and and_3 (and_3_out, d_ff_3_qn, I);
  and and_4 (and_4_out, d_ff_3_q, not_1_out);
  and and_5 (and_5_out, d_ff_2_qn, d_ff_1_q);
  and and_6 (and_6_out, d_ff_2_q, d_ff_1_qn);
  and and_7 (and_7_out, d_ff_1_qn, d_ff_3_q);
  and and_8 (and_8_out, d_ff_1_q, d_ff_3_qn);
  or or_1 (or_1_out, and_1_out, and_2_out);
  or or_2 (or_2_out, and_3_out, and_4_out);
  or or_3 (or_3_out, and_5_out, and_6_out);
  and and_9 (and_9_out, or_3_out, and_10_out);
  and and_10 (and_10_out, d_ff_3_q, I);
  and and_11 (and_11_out, not_1_out, d_ff_3_qn, d_ff_2_q, d_ff_1_qn);
  or or_4 (or_4_out, and_7_out, and_8_out);
  and and_12 (and_12_out, d_ff_3_qn, not_1_out);
  and and_13 (and_13_out, d_ff_1_qn, d_ff_2_q);
  or or_5 (or_5_out, and_9_out, and_11_out);
  and and_14 (and_14_out, d_ff_2_qn, or_4_out);
  or or_6 (or_6_out, and_14_out, and_15_out);
  and and_15 (and_15_out, d_ff_1_qn, d_ff_2_q, d_ff_3_qn, I);
  and and_16 (and_16_out, and_12_out, or_1_out);
  or or_7 (or_7_out, and_16_out, and_17_out);
  and and_17 (and_17_out, and_13_out, or_2_out);
  D_Flip_Flop d_ff_1 (.D(or_5_out), .clk(clock_1_out), .Q(d_ff_1_q), .Qn(d_ff_1_qn));  // open: preset, reset
  D_Flip_Flop d_ff_2 (.D(or_6_out), .clk(clock_1_out), .Q(d_ff_2_q), .Qn(d_ff_2_qn));  // open: preset, reset
  D_Flip_Flop d_ff_3 (.D(or_7_out), .clk(clock_1_out), .Q(d_ff_3_q), .Qn(d_ff_3_qn));  // open: preset, reset
  and and_18 (and_18_out, d_ff_1_q, not_1_out, d_ff_2_qn, d_ff_3_qn);
  and and_19 (and_19_out, d_ff_1_q, d_ff_2_qn, d_ff_3_q, I);
  or or_8 (Unlock, and_18_out, and_19_out);
endmodule
