// Logisim project version1.circ as structural Verilog: 2 circuits, main circuit main
module main (
  input  [3:0] Value,
  input  [1:0] FN,
  input  GO,
  output out_4
);

  wire and_1_out, clock_1_out, d_ff_1_qn;

  Clock clock_1 (.out(clock_1_out));
  D_Flip_Flop d_ff_1 (.D(GO), .clk(clock_1_out), .Qn(d_ff_1_qn));  // open: Q, preset, reset
  Register #(.width(4)) register_1 (.en(and_1_out), .clk(clock_1_out));  // open: D, Q, clr
  and and_1 (and_1_out, GO, d_ff_1_qn);
endmodule

module calc (
  input  [1:0] MathFunc,
  input  [3:0] InValue,
  input  GO,
  output [3:0] Result
);

  wire and_1_out, clock_1_out, d_ff_1_qn;
  wire [3:0] adder_1_out, multiplexer_1_out, multiplier_1_out, subtractor_1_out;

  Clock clock_1 (.out(clock_1_out));
  D_Flip_Flop d_ff_1 (.D(GO), .clk(clock_1_out), .Qn(d_ff_1_qn));  // open: Q, preset, reset
  Register #(.width(4)) register_1 (.D(multiplexer_1_out), .en(and_1_out), .clk(clock_1_out), .Q(Result));  // open: clr
  Adder #(.width(4)) adder_1 (.a(Result), .b(InValue), .out(adder_1_out));  // open: cin, cout
  Subtractor #(.width(4)) subtractor_1 (.a(Result), .b(InValue), .out(subtractor_1_out));  // open: bin, bout
  Multiplier #(.width(4)) multiplier_1 (.a(Result), .b(InValue), .out(multiplier_1_out));  // open: cin, cout
  and and_1 (and_1_out, GO, d_ff_1_qn);
  Multiplexer #(.select(2), .width(4)) multiplexer_1 (
    .in0(InValue), .in1(adder_1_out), .in2(subtractor_1_out), .in3(multiplier_1_out),
    .out(multiplexer_1_out), .sel(MathFunc));
endmodule
