// Logisim project Lab10.circ as structural Verilog: 4 circuits, main circuit datapath
module control_unit (
  input  RESET,
  input  CD,
  input  EN_COUNT,
  input  [2:0] HWL,
  input  [2:0] FL,
  output [3:0] TICK_CNT,
  output EN,
  output [2:0] HWSL,
  output [2:0] FRSL
);

  wire and_1_out, and_2_out, and_3_out, clock_1_out, multiplexer_2_out, multiplexer_3_out, multiplexer_4_out,
       multiplexer_5_out, multiplexer_6_out, multiplexer_7_out, or_1_out, or_2_out, or_3_out;
  wire [3:0] adder_1_out, multiplexer_1_out;

  or or_1 (or_1_out, EN, RESET);
  Clock clock_1 (.out(clock_1_out));
  LED led_1 (.in(HWL[0]));
  LED led_2 (.in(HWL[1]));
  LED led_3 (.in(HWL[2]));
  LED led_4 (.in(FL[0]));
  LED led_5 (.in(FL[1]));
  LED led_6 (.in(FL[2]));
  Adder #(.width(4)) adder_1 (.a(TICK_CNT), .b(4'b0001), .out(adder_1_out));  // open: cin, cout
  Multiplexer #(.width(4)) multiplexer_1 (.in0(adder_1_out), .in1(4'b0000), .out(multiplexer_1_out), .sel(or_1_out));
  Register #(.width(4)) register_1 (
    .D(multiplexer_1_out), .en(EN_COUNT), .clk(clock_1_out), .Q(TICK_CNT), .clr(or_1_out));
  Subtractor subtractor_1 ();  // open: a, b, out, bin, bout
  Multiplexer #(.select(4)) multiplexer_2 (
    .in0(1'b0), .in1(1'b0), .in2(1'b0), .in3(1'b1), .in4(1'b0), .in5(1'b0), .in6(1'b0), .in7(1'b0),
    .in8(1'b0), .in9(1'b0), .in10(1'b0), .in11(1'b0), .in12(1'b0), .in13(1'b0), .in14(1'b0), .in15(1'b0),
    .out(multiplexer_2_out), .sel(TICK_CNT));
  Multiplexer #(.select(4)) multiplexer_3 (
    .in0(1'b0), .in1(1'b0), .in2(1'b0), .in3(1'b0), .in4(1'b0), .in5(1'b0), .in6(1'b0), .in7(1'b0),
    .in8(1'b0), .in9(1'b0), .in10(1'b0), .in11(1'b0), .in12(1'b0), .in13(1'b0), .in14(1'b0), .in15(1'b1),
    .out(multiplexer_3_out), .sel(TICK_CNT));
  Multiplexer #(.select(3)) multiplexer_4 (
    .in0(1'b0), .in1(1'b1), .in2(1'b0), .in3(1'b0), .in4(1'b0), .in5(1'b0), .in6(1'b0), .in7(1'b0),
    .out(multiplexer_4_out), .sel(HWL));
  Multiplexer #(.select(3)) multiplexer_5 (
    .in0(1'b0), .in1(1'b0), .in2(1'b1), .in3(1'b0), .in4(1'b0), .in5(1'b0), .in6(1'b0), .in7(1'b0),
    .out(multiplexer_5_out), .sel(FL));
  Multiplexer #(.select(3)) multiplexer_6 (
    .in0(1'b0), .in1(1'b0), .in2(1'b1), .in3(1'b0), .in4(1'b0), .in5(1'b0), .in6(1'b0), .in7(1'b0),
    .out(multiplexer_6_out), .sel(HWL));
  or or_2 (or_2_out, multiplexer_5_out, multiplexer_6_out);
  or or_3 (or_3_out, multiplexer_7_out, and_1_out);
  and and_1 (and_1_out, CD, multiplexer_4_out);
  Multiplexer #(.select(3)) multiplexer_7 (
    .in0(1'b0), .in1(1'b1), .in2(1'b0), .in3(1'b0), .in4(1'b0), .in5(1'b0), .in6(1'b0), .in7(1'b0),
    .out(multiplexer_7_out), .sel(FL));
  and and_2 (and_2_out, or_2_out, multiplexer_2_out);
  and and_3 (and_3_out, multiplexer_3_out, or_3_out);
  or or_4 (EN, and_2_out, and_3_out);

  assign FRSL = FL;
  assign HWSL = HWL;

  // Notes on the sheet:
  //   Enable Feedback
  //   Counter: Q + 1
  //   3 cycles Mux
  //   16 cycles Mux
  //   HWL Mux
  //   HWL Mux
  //   FRL Mux
  //   C.0x3(HWL.0x3 + FRL.0x3)
  //   (FRL: Yellow or HWL: Yellow) & 3 Cycles
  //   (HWL: Red or FRL: Red) & 16 Cycles
  //   =(C.0xf)(HWL.0x1 or FRL.0x1)
endmodule

module datapath (
  input  RESET,
  input  Timer_EN,
  output [2:0] HWL,
  output [2:0] FRL
);

  wire and_1_out, and_2_out, and_3_out, clock_1_out, multiplexer_1_out, not_1_out, not_2_out, or_1_out,
       xor_1_out;
  wire [1:0] R0_q;

  Clock clock_1 (.out(clock_1_out));
  and and_1 (and_1_out, Timer_EN, clock_1_out);
  Multiplexer #(.select(2)) multiplexer_1 (
    .in0(1'b1), .in1(R0_q[0]), .in2(1'b0), .in3(1'b0), .out(multiplexer_1_out), .sel(R0_q));
  Register #(.width(1)) R1 (.D(multiplexer_1_out), .en(xor_1_out), .clk(and_1_out), .Q(R0_q[1]), .clr(RESET));
  Register #(.width(1)) R0 (.D(multiplexer_1_out), .en(or_1_out), .clk(and_1_out), .Q(R0_q[0]), .clr(RESET));
  xor xor_1 (xor_1_out, R0_q[1], R0_q[0]);
  not not_1 (not_1_out, R0_q[1]);
  not not_2 (not_2_out, R0_q[0]);
  and and_2 (and_2_out, R0_q[1], R0_q[0]);
  or or_1 (or_1_out, and_2_out, and_3_out);
  and and_3 (and_3_out, not_1_out, not_2_out);
  Multiplexer #(.select(2), .width(3)) multiplexer_2 (
    .in0(3'b001), .in1(3'b010), .in2(3'b100), .in3(3'b100), .out(HWL), .sel(R0_q));
  Multiplexer #(.select(2), .width(3)) multiplexer_3 (
    .in0(3'b100), .in1(3'b100), .in2(3'b010), .in3(3'b001), .out(FRL), .sel(R0_q));
  LED led_1 (.in(HWL[0]));
  LED led_2 (.in(HWL[1]));
  LED led_3 (.in(HWL[2]));
  LED led_4 (.in(FRL[0]));
  LED led_5 (.in(FRL[1]));
  LED led_6 (.in(FRL[2]));

  // Notes on the sheet:
  //   Functional version of data path
endmodule

module main (
  input  CD,
  input  RESET,
  input  EN_COUNT_FIXME,
  output [2:0] HWL,
  output [3:0] out_5,
  output [2:0] FRL,
  output [2:0] out_7,
  output [2:0] out_8
);

  wire control_unit_1_en;

  control_unit control_unit_1 (
    .RESET(RESET), .CD(CD), .EN_COUNT(EN_COUNT_FIXME), .HWL(HWL), .FL(FRL), .TICK_CNT(out_5),
    .EN(control_unit_1_en), .HWSL(out_7), .FRSL(out_8));
  datapath datapath_1 (.RESET(RESET), .Timer_EN(control_unit_1_en), .HWL(HWL), .FRL(FRL));
  LED led_1 (.in(HWL[0]));
  LED led_2 (.in(HWL[1]));
  LED led_3 (.in(HWL[2]));
  LED led_4 (.in(FRL[0]));
  LED led_5 (.in(FRL[1]));
  LED led_6 (.in(FRL[2]));
endmodule

module latch_proto (
  input  CD,
  output [6:0] TICK_CNT,
  output LATCH
);

  wire clock_1_out, not_1_out, not_2_out, not_3_out, not_4_out, not_5_out;
  wire [6:0] adder_1_out, multiplexer_1_out;

  Clock clock_1 (.out(clock_1_out));
  Adder #(.width(7)) adder_1 (.a(TICK_CNT), .b(7'b0000001), .out(adder_1_out));  // open: cin, cout
  Multiplexer #(.width(7)) multiplexer_1 (.in0({7{1'b0}}), .in1(adder_1_out), .out(multiplexer_1_out), .sel(CD));
  Register #(.width(7)) register_1 (.D(multiplexer_1_out), .en(CD), .clk(clock_1_out), .Q(TICK_CNT), .clr(LATCH));
  not not_1 (not_1_out, TICK_CNT[6]);
  not not_2 (not_2_out, TICK_CNT[4]);
  not not_3 (not_3_out, TICK_CNT[2]);
  not not_4 (not_4_out, TICK_CNT[1]);
  and and_1 (LATCH, not_1_out, TICK_CNT[5], not_2_out, TICK_CNT[3], not_3_out, not_4_out, not_5_out);
  not not_5 (not_5_out, TICK_CNT[0]);
  // NOT_Gate not_6 is placed but not wired

  // Notes on the sheet:
  //   Counter: Q + 1
endmodule
