// Logisim project Lab9.circ as structural Verilog: 3 circuits, main circuit version3
module main (
  input  Func,
  input  Pwr,
  output [2:0] HL,
  output [2:0] FL
);

  wire clock_1_out;
  wire [2:0] register_1_q, register_2_q, shifter_1_out, shifter_2_out;

  Clock clock_1 (.out(clock_1_out));
  Shifter #(.shift("rl"), .width(3)) shifter_1 (.in(HL), .\dist (2'b01), .out(shifter_1_out));
  Shifter #(.shift("rl"), .width(3)) shifter_2 (.in(FL), .\dist (2'b01), .out(shifter_2_out));
  Register #(.width(3)) register_1 (.D(shifter_1_out), .en(Pwr), .clk(clock_1_out), .Q(register_1_q));  // open: clr
  Register #(.width(3)) register_2 (.D(shifter_2_out), .en(Pwr), .clk(clock_1_out), .Q(register_2_q));  // open: clr
  Multiplexer #(.width(3)) multiplexer_1 (.in0(3'b001), .in1(register_1_q), .out(HL), .sel(Func));
  Multiplexer #(.width(3)) multiplexer_2 (.in0(3'b100), .in1(register_2_q), .out(FL), .sel(Func));
  LED led_1 (.in(HL[0]));
  LED led_2 (.in(HL[1]));
  LED led_3 (.in(HL[2]));
  LED led_4 (.in(FL[0]));
  LED led_5 (.in(FL[1]));
  LED led_6 (.in(FL[2]));
endmodule

module version2 (
  input  CHNGE,
  output [2:0] FRL,
  output [2:0] HWL
);

  wire clock_1_out, not_1_out;
  wire [2:0] FR_q, HW_q, shifter_1_out;

  Clock clock_1 (.out(clock_1_out));
  Shifter #(.shift("rl"), .width(3)) shifter_1 (.in(FRL), .\dist (2'b01), .out(shifter_1_out));
  Register #(.width(3)) FR (.D(shifter_1_out), .en(CHNGE), .clk(clock_1_out), .Q(FR_q));  // open: clr
  Register #(.width(3)) HW (.D(HWL), .en(CHNGE), .clk(clock_1_out), .Q(HW_q));  // open: clr
  Multiplexer #(.width(3)) multiplexer_1 (.in0(3'b100), .in1(FR_q), .out(FRL), .sel(not_1_out));
  not not_1 (not_1_out, CHNGE);
  Multiplexer #(.width(3)) multiplexer_2 (.in0(3'b001), .in1(HW_q), .out(HWL), .sel(CHNGE));
  LED led_1 (.in(FRL[0]));
  LED led_2 (.in(FRL[1]));
  LED led_3 (.in(FRL[2]));
  LED led_4 (.in(HWL[0]));
  LED led_5 (.in(HWL[1]));
  LED led_6 (.in(HWL[2]));
endmodule

module version3 (
  input  CD,
  input  RESET,
  output [2:0] HWL,
  output [2:0] FRL
);

  wire and_1_out, and_2_out, clock_1_out, multiplexer_1_out, not_1_out, not_2_out, or_1_out, xor_1_out;
  wire [1:0] R0_q;

  Clock clock_1 (.out(clock_1_out));
  Multiplexer #(.select(2)) multiplexer_1 (
    .in0(1'b1), .in1(R0_q[0]), .in2(1'b0), .in3(1'b0), .out(multiplexer_1_out), .sel(R0_q));
  Register #(.width(1)) R1 (.D(multiplexer_1_out), .en(xor_1_out), .clk(clock_1_out), .Q(R0_q[1]), .clr(RESET));
  Register #(.width(1)) R0 (.D(multiplexer_1_out), .en(or_1_out), .clk(clock_1_out), .Q(R0_q[0]), .clr(RESET));
  xor xor_1 (xor_1_out, R0_q[1], R0_q[0]);
  not not_1 (not_1_out, R0_q[1]);
  not not_2 (not_2_out, R0_q[0]);
  and and_1 (and_1_out, R0_q[1], R0_q[0]);
  or or_1 (or_1_out, and_1_out, and_2_out);
  and and_2 (and_2_out, not_1_out, not_2_out);
  Multiplexer #(.select(2), .width(3)) multiplexer_2 (
    .in0(3'b001), .in1(3'b010), .in2(3'b100), .in3(3'b100), .out(HWL), .sel(R0_q));
  Multiplexer #(.select(2), .width(3)) multiplexer_3 (
    .in0(3'b100), .in1(3'b100), .in2(3'b010), .in3(3'b001), .out(FRL), .sel(R0_q));
  LED led_1 (.in(HWL[0]));
  LED led_2 (.in(HWL[1]));
  LED led_3 (.in(HWL[2]));
  LED led_4 (.in(FRL[0]));
  LED led_5 (.in(FRL[1]));
  LED led_6 (.in(FRL[2]));

  // Notes on the sheet:
  //   Functional version of data path
endmodule
