// Logisim project Lab_11.circ as structural Verilog: 5 circuits, main circuit function_unit
module function_unit (
  input  [3:0] a_in,
  input  [3:0] b_in,
  input  [3:0] FS,
  output [2:0] PZN,
  output [3:0] F
);

  wire [3:0] adder_1_out, adder_2_out, and_1_out, divider_1_out, multiplier_1_out, negator_1_out,
       negator_2_out, or_1_out, shifter_1_out, shifter_2_out, shifter_3_out, subtractor_1_out;

  Adder #(.width(4)) adder_1 (.a(a_in), .b(b_in), .out(adder_1_out));  // open: cin, cout
  Subtractor #(.width(4)) subtractor_1 (.a(a_in), .b(b_in), .out(subtractor_1_out));  // open: bin, bout
  Multiplier #(.mode("twosComplement"), .width(4)) multiplier_1 (
    .a(a_in), .b(b_in), .out(multiplier_1_out));  // open: cin, cout
  Divider #(.mode("twosComplement"), .width(4)) divider_1 (
    .a(a_in), .b(b_in), .out(divider_1_out));  // open: upper, rem
  Negator #(.width(4)) negator_1 (.in(a_in), .out(negator_1_out));
  assign and_1_out = a_in & b_in;  // AND_Gate and_1, 4 bits wide
  assign or_1_out = a_in | b_in;  // OR_Gate or_1, 4 bits wide
  Negator #(.width(4)) negator_2 (.in(a_in), .out(negator_2_out));
  Shifter #(.shift("lr"), .width(4)) shifter_1 (.in(a_in), .\dist (2'b01), .out(shifter_1_out));
  Shifter #(.width(4)) shifter_2 (.in(a_in), .\dist (2'b01), .out(shifter_2_out));
  Shifter #(.shift("ar"), .width(4)) shifter_3 (.in(a_in), .\dist (2'b01), .out(shifter_3_out));
  Adder #(.width(4)) adder_2 (.a(negator_2_out), .b(4'b0001), .out(adder_2_out));  // open: cin, cout
  Multiplexer #(.select(4), .width(4)) multiplexer_1 (
    .in0(4'b0000), .in1(4'b0001), .in2(a_in), .in3(b_in), .in4(adder_1_out), .in5(subtractor_1_out),
    .in6(multiplier_1_out), .in7(divider_1_out), .in8(negator_1_out), .in9(and_1_out), .in10(or_1_out),
    .in11(adder_2_out), .in12(shifter_1_out), .in13(shifter_2_out), .in14(shifter_3_out), .out(F), .sel(FS));  // open: in15
  Comparator #(.width(4)) comparator_1 (.a(F), .b(4'b0000), .gt(PZN[2]), .eq(PZN[1]), .lt(PZN[0]));
endmodule

module datapath (
  input  [15:0] Control_Word,
  input  [3:0] constIn,
  input  [3:0] DataIn,
  output [3:0] AddrOut,
  output [3:0] DataOut,
  output [2:0] PZN
);

  wire clock_1_out;
  wire [3:0] function_unit_1_f, multiplexer_2_out, regfile_1_bout;

  Clock clock_1 (.out(clock_1_out));
  Multiplexer #(.width(4)) multiplexer_1 (.in0(regfile_1_bout), .in1(constIn), .out(DataOut), .sel(Control_Word[12]));
  Multiplexer #(.width(4)) multiplexer_2 (
    .in0(function_unit_1_f), .in1(DataIn), .out(multiplexer_2_out), .sel(Control_Word[8]));
  RegFile regfile_1 (
    .D_IN(multiplexer_2_out), .RW(Control_Word[0]), .DA(Control_Word[3:1]), .CLK(clock_1_out),
    .AA(Control_Word[15:13]), .BA(Control_Word[11:9]), .AOut(AddrOut), .BOut(regfile_1_bout));
  function_unit function_unit_1 (
    .a_in(AddrOut), .b_in(DataOut), .FS(Control_Word[7:4]), .PZN(PZN), .F(function_unit_1_f));

  // Notes on the sheet:
  //   D Address
  //   A Address
  //   B Address
  //   ConstIn
  //   RegfileWrite
  //   Function Select
  //   BOut
  //   MuxB
  //   Mux F
  //   Data In
  //   AOut
endmodule

module RegFile (
  input  [3:0] D_IN,
  input  RW,
  input  [2:0] DA,
  input  CLK,
  input  [2:0] AA,
  input  [2:0] BA,
  output [3:0] AOut,
  output [3:0] BOut
);

  wire and_1_out, and_2_out, and_3_out, and_4_out, and_5_out, and_6_out, and_7_out, and_8_out,
       decoder_1_out0, decoder_1_out1, decoder_1_out2, decoder_1_out3, decoder_1_out4, decoder_1_out5,
       decoder_1_out6, decoder_1_out7;
  wire [3:0] R0_q, R1_q, R2_q, R3_q, R4_q, R5_q, R6_q, R7_q;

  Decoder #(.enable("false"), .select(3)) decoder_1 (
    .out0(decoder_1_out0), .out1(decoder_1_out1), .out2(decoder_1_out2), .out3(decoder_1_out3),
    .out4(decoder_1_out4), .out5(decoder_1_out5), .out6(decoder_1_out6), .out7(decoder_1_out7), .sel(DA));
  Register #(.width(4)) R0 (.D(D_IN), .en(and_1_out), .clk(CLK), .Q(R0_q));  // open: clr
  and and_1 (and_1_out, decoder_1_out0, RW);
  Register #(.width(4)) R1 (.D(D_IN), .en(and_2_out), .clk(CLK), .Q(R1_q));  // open: clr
  and and_2 (and_2_out, decoder_1_out1, RW);
  Register #(.width(4)) R2 (.D(D_IN), .en(and_3_out), .clk(CLK), .Q(R2_q));  // open: clr
  and and_3 (and_3_out, decoder_1_out2, RW);
  Register #(.width(4)) R3 (.D(D_IN), .en(and_4_out), .clk(CLK), .Q(R3_q));  // open: clr
  and and_4 (and_4_out, decoder_1_out3, RW);
  Register #(.width(4)) R4 (.D(D_IN), .en(and_5_out), .clk(CLK), .Q(R4_q));  // open: clr
  and and_5 (and_5_out, decoder_1_out4, RW);
  Register #(.width(4)) R5 (.D(D_IN), .en(and_6_out), .clk(CLK), .Q(R5_q));  // open: clr
  and and_6 (and_6_out, decoder_1_out5, RW);
  Register #(.width(4)) R6 (.D(D_IN), .en(and_7_out), .clk(CLK), .Q(R6_q));  // open: clr
  and and_7 (and_7_out, decoder_1_out6, RW);
  Register #(.width(4)) R7 (.D(D_IN), .en(and_8_out), .clk(CLK), .Q(R7_q));  // open: clr
  and and_8 (and_8_out, decoder_1_out7, RW);
  Multiplexer #(.select(3), .width(4)) multiplexer_1 (
    .in0(R7_q), .in1(R6_q), .in2(R5_q), .in3(R4_q), .in4(R3_q), .in5(R2_q), .in6(R1_q), .in7(R0_q),
    .out(AOut), .sel(AA));
  Multiplexer #(.select(3), .width(4)) multiplexer_2 (
    .in0(R0_q), .in1(R1_q), .in2(R2_q), .in3(R3_q), .in4(R4_q), .in5(R5_q), .in6(R6_q), .in7(R7_q),
    .out(BOut), .sel(BA));
endmodule

module control_unit (
  input  [15:0] Instruction,
  input  Start,
  input  [2:0] PZN,
  input  Clock_in,
  input  [2:0] Condition,
  input  Reset
);

  wire clock_1_out, or_1_out;
  wire [2:0] and_1_out, register_1_q;

  Clock clock_1 (.out(clock_1_out));
  Counter #(.max('h1), .width(1)) counter_1 (.clr(Reset), .clk(clock_1_out));  // open: load, up, count, D, carry, Q
  Register #(.width(3)) register_1 (.D(PZN), .en(1'b1), .clk(Clock_in), .Q(register_1_q));  // open: clr
  assign and_1_out = register_1_q & Condition;  // AND_Gate and_1, 3 bits wide
  or or_1 (or_1_out, and_1_out[0], and_1_out[1], and_1_out[2]);
  ROM #(.dataWidth(18)) rom_1 ();  // open: addr, data

  // Notes on the sheet:
  //   Comparing PZN previous value
endmodule

module Instruction_encoder (
  input  MemoryWrite,
  input  [2:0] A_Address,
  input  MuxB,
  input  Mode,
  input  [2:0] B_Address,
  input  MuxF,
  input  [3:0] Func,
  input  [2:0] Dest_Address,
  input  RegfileWrite,
  input  [2:0] Condition,
  input  [7:0] Next_Address,
  output [17:0] Jump_code
);

  Multiplexer #(.width(17)) multiplexer_1 (
    .in0({MemoryWrite, A_Address, MuxB, B_Address, MuxF, Func, Dest_Address, RegfileWrite}),
    .in1({2'b00, Condition, Next_Address, 4'b0000}), .out(Jump_code[16:0]), .sel(Mode));

  assign Jump_code[17] = Mode;

  // Notes on the sheet:
  //   Mode 0 Block
  //   Mode 1 Block
endmodule
